# Fritzing sketch Smack Circuit (saved by Fritzing 0.9.3b)
stripboards: 1

parts:
  SparkFun_Micro_OLED_Breakout1 = SparkFun Micro OLED Breakout [part_number=LCD-13003]
  Part1 = Arduino Nano (Rev3.0) (ICSP)
  AUDIO_OUT = Audio Jack (TRRS) 3.5mm [part_number="LUMBERG JEITA RC-5325A" package="RC-5325A [SMD]"]  # not connected
  TRIG_IN = Audio Jack (TRRS) 3.5mm [part_number="LUMBERG JEITA RC-5325A" package="RC-5325A [SMD]"]
  Part2 = MP3 Trigger
  PITCH = POT [package=alps_pot]
  SAMPLE = POT [package=alps_pot]
  R1 = Resistor [tolerance=±5% resistance=220 package="0603 [SMD]"]
  R2 = Resistor [tolerance=±5% resistance=220 package="0603 [SMD]"]
  R3 = Resistor [tolerance=±5% resistance=220 package="0603 [SMD]"]

nets:
  GND: SparkFun_Micro_OLED_Breakout1.GND, Part1.GND, Part2.GND, R1.Pin_1, R2.Pin_1, R3.Pin_1
  VDD: SparkFun_Micro_OLED_Breakout1.VDD, Part1.3V3
  N1: SparkFun_Micro_OLED_Breakout1.D1/MOSI, Part1.D11/MOSI
  N2: SparkFun_Micro_OLED_Breakout1.D0/SCK, Part1.D13/SCK
  N3: SparkFun_Micro_OLED_Breakout1.D/C, Part1.D8
  N4: SparkFun_Micro_OLED_Breakout1.RESET, Part1.D6
  N5: SparkFun_Micro_OLED_Breakout1.CS, Part1.D10
  N6: Part1.D2, TRIG_IN.TIP, R1.Pin_0
  N7: Part1.D9, Part2.RX-I
  N8: Part1.5V, Part2.USBVCC, PITCH.S, SAMPLE.S
  N9: Part1.A7, PITCH.E, R2.Pin_0
  N10: Part1.A1, SAMPLE.E, R3.Pin_0

custom parts:
  SparkFun Micro OLED Breakout: Description: The SparkFun Micro OLED Breakout Board breaks out a small monochrome, blue-on-black OLED. It’s “micro”, but it still packs a punch – the OLED display is crisp, and you can fit a deceivingly large amount of graphics on there. This breakout is perfect for adding graphics to your next Arduino project, displaying diagnostic information without resorting to serial output, and teaching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
